// Logisim project projeto.circ as structural Verilog: 4 circuits, main circuit main
module main (
  input  in_1,
  input  in_2,
  input  in_3,
  input  in_4,
  input  in_5,
  output out_6,
  output out_7,
  output out_8,
  output out_9,
  output out_10
);

  wire codificador2_1_e0, codificador2_1_e1, codificador2_1_e2, codificador2_1_e3, codificador2_1_j0,
       codificador2_1_j1, codificador2_1_j2, codificador2_1_j3, codificador2_1_o0, codificador2_1_o1,
       codificador2_1_o2, codificador2_1_o3, codificador2_1_s0, codificador2_1_s1, codificador2_1_s2,
       codificador2_1_s3, codificador2_1_u0, codificador2_1_u1, codificador2_1_u2, codificador2_1_u3,
       decodificador_7_segmentos_1_a_2, decodificador_7_segmentos_1_b_2, decodificador_7_segmentos_1_c_2,
       decodificador_7_segmentos_1_d_2, decodificador_7_segmentos_1_e, decodificador_7_segmentos_1_f,
       decodificador_7_segmentos_1_g, decodificador_7_segmentos_2_a_2, decodificador_7_segmentos_2_b_2,
       decodificador_7_segmentos_2_c_2, decodificador_7_segmentos_2_d_2, decodificador_7_segmentos_2_e,
       decodificador_7_segmentos_2_f, decodificador_7_segmentos_2_g, decodificador_7_segmentos_3_a_2,
       decodificador_7_segmentos_3_b_2, decodificador_7_segmentos_3_c_2, decodificador_7_segmentos_3_d_2,
       decodificador_7_segmentos_3_e, decodificador_7_segmentos_3_f, decodificador_7_segmentos_3_g,
       decodificador_7_segmentos_4_a_2, decodificador_7_segmentos_4_b_2, decodificador_7_segmentos_4_c_2,
       decodificador_7_segmentos_4_d_2, decodificador_7_segmentos_4_e, decodificador_7_segmentos_4_f,
       decodificador_7_segmentos_4_g, decodificador_7_segmentos_5_a_2, decodificador_7_segmentos_5_b_2,
       decodificador_7_segmentos_5_c_2, decodificador_7_segmentos_5_d_2, decodificador_7_segmentos_5_e,
       decodificador_7_segmentos_5_f, decodificador_7_segmentos_5_g;

  decodificador_7_segmentos decodificador_7_segmentos_1 (
    .A(codificador2_1_j0), .B(codificador2_1_j1), .C(codificador2_1_j2), .D(codificador2_1_j3),
    .a_2(decodificador_7_segmentos_1_a_2), .b_2(decodificador_7_segmentos_1_b_2),
    .c_2(decodificador_7_segmentos_1_c_2), .d_2(decodificador_7_segmentos_1_d_2),
    .e(decodificador_7_segmentos_1_e), .f(decodificador_7_segmentos_1_f), .g(decodificador_7_segmentos_1_g));
  _7_Segment_Display u_7_segment_display_1 (
    .g(decodificador_7_segmentos_1_g), .f(decodificador_7_segmentos_1_f),
    .a(decodificador_7_segmentos_1_a_2), .b(decodificador_7_segmentos_1_b_2),
    .e(decodificador_7_segmentos_1_e), .d(decodificador_7_segmentos_1_d_2),
    .c(decodificador_7_segmentos_1_c_2));  // open: dp
  decodificador_7_segmentos decodificador_7_segmentos_2 (
    .A(codificador2_1_o0), .B(codificador2_1_o1), .C(codificador2_1_o2), .D(codificador2_1_o3),
    .a_2(decodificador_7_segmentos_2_a_2), .b_2(decodificador_7_segmentos_2_b_2),
    .c_2(decodificador_7_segmentos_2_c_2), .d_2(decodificador_7_segmentos_2_d_2),
    .e(decodificador_7_segmentos_2_e), .f(decodificador_7_segmentos_2_f), .g(decodificador_7_segmentos_2_g));
  _7_Segment_Display u_7_segment_display_2 (
    .g(decodificador_7_segmentos_2_g), .f(decodificador_7_segmentos_2_f),
    .a(decodificador_7_segmentos_2_a_2), .b(decodificador_7_segmentos_2_b_2),
    .e(decodificador_7_segmentos_2_e), .d(decodificador_7_segmentos_2_d_2),
    .c(decodificador_7_segmentos_2_c_2));  // open: dp
  codificador2 codificador2_1 (
    .J(in_1), .O(in_2), .S(in_3), .U(in_4), .E(in_5), .J0(codificador2_1_j0), .J1(codificador2_1_j1),
    .J2(codificador2_1_j2), .J3(codificador2_1_j3), .o0(codificador2_1_o0), .o1(codificador2_1_o1),
    .o2(codificador2_1_o2), .o3(codificador2_1_o3), .S0(codificador2_1_s0), .S1(codificador2_1_s1),
    .S2(codificador2_1_s2), .S3(codificador2_1_s3), .U0(codificador2_1_u0), .U1(codificador2_1_u1),
    .U2(codificador2_1_u2), .U3(codificador2_1_u3), .E0(codificador2_1_e0), .E1(codificador2_1_e1),
    .E2(codificador2_1_e2), .E3(codificador2_1_e3));
  decodificador_7_segmentos decodificador_7_segmentos_3 (
    .A(codificador2_1_s0), .B(codificador2_1_s1), .C(codificador2_1_s2), .D(codificador2_1_s3),
    .a_2(decodificador_7_segmentos_3_a_2), .b_2(decodificador_7_segmentos_3_b_2),
    .c_2(decodificador_7_segmentos_3_c_2), .d_2(decodificador_7_segmentos_3_d_2),
    .e(decodificador_7_segmentos_3_e), .f(decodificador_7_segmentos_3_f), .g(decodificador_7_segmentos_3_g));
  _7_Segment_Display u_7_segment_display_3 (
    .g(decodificador_7_segmentos_3_g), .f(decodificador_7_segmentos_3_f),
    .a(decodificador_7_segmentos_3_a_2), .b(decodificador_7_segmentos_3_b_2),
    .e(decodificador_7_segmentos_3_e), .d(decodificador_7_segmentos_3_d_2),
    .c(decodificador_7_segmentos_3_c_2));  // open: dp
  decodificador_7_segmentos decodificador_7_segmentos_4 (
    .A(codificador2_1_u0), .B(codificador2_1_u1), .C(codificador2_1_u2), .D(codificador2_1_u3),
    .a_2(decodificador_7_segmentos_4_a_2), .b_2(decodificador_7_segmentos_4_b_2),
    .c_2(decodificador_7_segmentos_4_c_2), .d_2(decodificador_7_segmentos_4_d_2),
    .e(decodificador_7_segmentos_4_e), .f(decodificador_7_segmentos_4_f), .g(decodificador_7_segmentos_4_g));
  _7_Segment_Display u_7_segment_display_4 (
    .g(decodificador_7_segmentos_4_g), .f(decodificador_7_segmentos_4_f),
    .a(decodificador_7_segmentos_4_a_2), .b(decodificador_7_segmentos_4_b_2),
    .e(decodificador_7_segmentos_4_e), .d(decodificador_7_segmentos_4_d_2),
    .c(decodificador_7_segmentos_4_c_2));  // open: dp
  decodificador_7_segmentos decodificador_7_segmentos_5 (
    .A(codificador2_1_e0), .B(codificador2_1_e1), .C(codificador2_1_e2), .D(codificador2_1_e3),
    .a_2(decodificador_7_segmentos_5_a_2), .b_2(decodificador_7_segmentos_5_b_2),
    .c_2(decodificador_7_segmentos_5_c_2), .d_2(decodificador_7_segmentos_5_d_2),
    .e(decodificador_7_segmentos_5_e), .f(decodificador_7_segmentos_5_f), .g(decodificador_7_segmentos_5_g));
  _7_Segment_Display u_7_segment_display_5 (
    .g(decodificador_7_segmentos_5_g), .f(decodificador_7_segmentos_5_f),
    .a(decodificador_7_segmentos_5_a_2), .b(decodificador_7_segmentos_5_b_2),
    .e(decodificador_7_segmentos_5_e), .d(decodificador_7_segmentos_5_d_2),
    .c(decodificador_7_segmentos_5_c_2));  // open: dp

  assign out_6 = in_1;
  assign out_7 = in_2;
  assign out_8 = in_3;
  assign out_9 = in_4;
  assign out_10 = in_5;
endmodule

// Decodificador 7 segmentos
module decodificador_7_segmentos (
  input  A,
  input  B,
  input  C,
  input  D,
  output a_2,
  output b_2,
  output c_2,
  output d_2,
  output e,
  output f,
  output g
);

  wire and_1_out, and_2_out, and_3_out, and_4_out, and_5_out, and_6_out, and_7_out, and_8_out, and_9_out,
       and_10_out, and_11_out, and_12_out, and_13_out, and_14_out, and_15_out, and_16_out, and_17_out,
       and_18_out, not_1_out, not_2_out, not_3_out, not_4_out, not_5_out, not_6_out, not_7_out, not_8_out,
       not_9_out, not_10_out, not_11_out, not_12_out, not_13_out, not_14_out, not_15_out, not_16_out,
       not_17_out, not_18_out, not_19_out, not_20_out, not_21_out, not_22_out, not_23_out, not_24_out,
       not_25_out, not_26_out, not_27_out, not_28_out, not_29_out, not_30_out, not_31_out, not_32_out,
       not_33_out, not_34_out, not_35_out, not_36_out, not_37_out, not_38_out, not_39_out, not_40_out,
       not_41_out;

  not not_1 (not_1_out, A);
  not not_2 (not_2_out, B);
  not not_3 (not_3_out, A);
  not not_4 (not_4_out, C);
  not not_5 (not_5_out, A);
  not not_6 (not_6_out, B);
  not not_7 (not_7_out, C);
  not not_8 (not_8_out, A);
  not not_9 (not_9_out, B);
  not not_10 (not_10_out, D);
  not not_11 (not_11_out, A);
  not not_12 (not_12_out, C);
  not not_13 (not_13_out, D);
  not not_14 (not_14_out, A);
  not not_15 (not_15_out, B);
  not not_16 (not_16_out, A);
  not not_17 (not_17_out, B);
  not not_18 (not_18_out, A);
  not not_19 (not_19_out, C);
  not not_20 (not_20_out, D);
  not not_21 (not_21_out, A);
  and and_1 (and_1_out, not_21_out, not_22_out, D);
  not not_22 (not_22_out, B);
  not not_23 (not_23_out, A);
  and and_2 (and_2_out, not_23_out, not_24_out, C);
  not not_24 (not_24_out, B);
  not not_25 (not_25_out, A);
  and and_3 (and_3_out, not_25_out, B, not_26_out);
  not not_26 (not_26_out, C);
  not not_27 (not_27_out, A);
  not not_28 (not_28_out, C);
  not not_29 (not_29_out, A);
  not not_30 (not_30_out, B);
  not not_31 (not_31_out, D);
  not not_32 (not_32_out, A);
  not not_33 (not_33_out, C);
  not not_34 (not_34_out, A);
  not not_35 (not_35_out, B);
  and and_4 (and_4_out, not_34_out, not_35_out, C);
  not not_36 (not_36_out, A);
  and and_5 (and_5_out, not_36_out, B, not_37_out);
  not not_37 (not_37_out, C);
  not not_38 (not_38_out, A);
  not not_39 (not_39_out, B);
  not not_40 (not_40_out, A);
  not not_41 (not_41_out, C);
  and and_6 (and_6_out, not_1_out, not_2_out, C);
  or or_1 (a_2, and_6_out, and_7_out);
  and and_7 (and_7_out, not_3_out, B, not_4_out, D);
  and and_8 (and_8_out, not_5_out, not_6_out, not_7_out, D);
  and and_9 (and_9_out, not_8_out, not_9_out, C, not_10_out);
  or or_2 (b_2, and_8_out, and_9_out, and_10_out);
  and and_10 (and_10_out, not_11_out, B, not_12_out, not_13_out);
  and and_11 (and_11_out, not_14_out, not_15_out, D);
  or or_3 (c_2, and_11_out, and_12_out, and_13_out);
  and and_12 (and_12_out, not_16_out, not_17_out, C);
  and and_13 (and_13_out, not_18_out, B, not_19_out, not_20_out);
  or or_4 (d_2, and_1_out, and_2_out, and_3_out);
  and and_14 (and_14_out, not_27_out, not_28_out, D);
  or or_5 (e, and_14_out, and_15_out, and_16_out);
  and and_15 (and_15_out, not_29_out, not_30_out, C, not_31_out);
  and and_16 (and_16_out, not_32_out, B, not_33_out);
  or or_6 (f, and_4_out, and_5_out);
  and and_17 (and_17_out, not_38_out, not_39_out, C, D);
  or or_7 (g, and_17_out, and_18_out);
  and and_18 (and_18_out, not_40_out, B, not_41_out, D);
endmodule

module Codificador (
  input  ch1,
  input  ch2,
  input  ch3,
  input  ch4,
  input  ch5,
  output A,
  output B,
  output C,
  output D
);

  or or_1 (B, ch4, ch5);
  or or_2 (C, ch2, ch3);
  or or_3 (D, ch1, ch3, ch5);

  assign A = 1'b0;
endmodule

// Codificador
module codificador2 (
  input  J,
  input  O,
  input  S,
  input  U,
  input  E,
  output J0,
  output J1,
  output J2,
  output J3,
  output o0,
  output o1,
  output o2,
  output o3,
  output S0,
  output S1,
  output S2,
  output S3,
  output U0,
  output U1,
  output U2,
  output U3,
  output E0,
  output E1,
  output E2,
  output E3
);

  Codificador codificador_1 (.ch1(J), .ch2(1'b0), .ch3(1'b0), .ch4(1'b0), .ch5(1'b0), .A(J0), .B(J1), .C(J2), .D(J3));
  Codificador codificador_2 (.ch1(1'b0), .ch2(O), .ch3(1'b0), .ch4(1'b0), .ch5(1'b0), .A(o0), .B(o1), .C(o2), .D(o3));
  Codificador codificador_3 (.ch1(1'b0), .ch2(1'b0), .ch3(S), .ch4(1'b0), .ch5(1'b0), .A(S0), .B(S1), .C(S2), .D(S3));
  Codificador codificador_4 (.ch1(1'b0), .ch2(1'b0), .ch3(1'b0), .ch4(U), .ch5(1'b0), .A(U0), .B(U1), .C(U2), .D(U3));
  Codificador codificador_5 (.ch1(1'b0), .ch2(1'b0), .ch3(1'b0), .ch4(1'b0), .ch5(E), .A(E0), .B(E1), .C(E2), .D(E3));
endmodule
